# Fritzing sketch AnalogReadSerial (saved by Fritzing 0.9.3b)
breadboards: 1

parts:
  Part1 = Arduino Uno (Rev3)
  U1 = POT [package=alps_pot]

nets:
  N1: Part1.A0, U1.S
  N2: Part1.5V, U1.A
  N3: Part1.GND, U1.E
